// Logisim project Mini_project_final.circ as structural Verilog: 11 circuits, main circuit main
module main (
  input  [31:0] num1,
  input  [31:0] num2,
  input  [31:0] num3,
  input  [31:0] num4,
  input  [31:0] num5,
  input  CLEAR,
  input  [31:0] num6,
  input  START,
  input  [31:0] num7,
  input  [31:0] num8,
  output [31:0] out_11,
  output [31:0] out_12,
  output [31:0] out_13,
  output [31:0] out_14,
  output [31:0] out_15,
  output [31:0] out_16,
  output [31:0] out_17,
  output [31:0] out_18
);

  wire and_1_out, CLK_out;

  Complete_Engine Sorting_engine (
    .Number_1(num1), .Number_2(num2), .Number_3(num3), .Number_4(num4), .Number_5(num5), .Number_6(num6),
    .Number_7(num7), .Number_8(num8), .Clear(CLEAR), .Clock(and_1_out), .F1(out_18), .F5(out_14),
    .F2(out_17), .F6(out_13), .F3(out_16), .F7(out_12), .F4(out_15), .F8(out_11));  // open: out_11, out_15, out_12, out_16, out_13, out_17, out_14, out_18
  and and_1 (and_1_out, START, CLK_out);
  Clock CLK (.out(CLK_out));

  // Other names for the same wires on the sheet: F1[31:0] = out_18; F2[31:0] = out_17; F3[31:0] = out_16;
  //   F4[31:0] = out_15; F5[31:0] = out_14; F6[31:0] = out_13; F7[31:0] = out_12; F8[31:0] = out_11; N1[31:0] = num1;
  //   N2[31:0] = num2; N3[31:0] = num3; N4[31:0] = num4; N5[31:0] = num5; N6[31:0] = num6; N7[31:0] = num7;
  //   N8[31:0] = num8

  // Notes on the sheet:
  //   INPUT
  //   USE CLK FREQ: 4hz
  //   CLEAR ONCE BEFORE START
  //   NOTE: ENABLE TICKS BEFORE YOU START!!
  //   OUTPUT
endmodule

module BLOCK (
  input  prev1,
  input  MSB1,
  input  prev2,
  input  MSB2,
  input  prev3,
  input  MSB3,
  input  prev4,
  input  MSB4,
  input  prev5,
  input  MSB5,
  input  prev6,
  input  MSB6,
  input  prev7,
  input  MSB7,
  input  prev8,
  input  MSB8,
  output O1,
  output O2,
  output O3,
  output O4,
  output O5,
  output O6,
  output O7,
  output O8
);

  wire M1, M2, M3, M4, M5, M6, M7, M8, or_1_out;

  and and_1 (M1, prev1, MSB1);
  and and_2 (M2, prev2, MSB2);
  and and_3 (M3, prev3, MSB3);
  and and_4 (M4, prev4, MSB4);
  and and_5 (M5, prev5, MSB5);
  and and_6 (M6, prev6, MSB6);
  and and_7 (M7, prev7, MSB7);
  and and_8 (M8, prev8, MSB8);
  Multiplexer #(.enable("false")) multiplexer_1 (.in0(prev1), .in1(M1), .out(O1), .sel(or_1_out));
  Multiplexer #(.enable("false")) multiplexer_2 (.in0(prev2), .in1(M2), .out(O2), .sel(or_1_out));
  Multiplexer #(.enable("false")) multiplexer_3 (.in0(prev3), .in1(M3), .out(O3), .sel(or_1_out));
  Multiplexer #(.enable("false")) multiplexer_4 (.in0(prev4), .in1(M4), .out(O4), .sel(or_1_out));
  Multiplexer #(.enable("false")) multiplexer_5 (.in0(prev5), .in1(M5), .out(O5), .sel(or_1_out));
  Multiplexer #(.enable("false")) multiplexer_6 (.in0(prev6), .in1(M6), .out(O6), .sel(or_1_out));
  Multiplexer #(.enable("false")) multiplexer_7 (.in0(prev7), .in1(M7), .out(O7), .sel(or_1_out));
  Multiplexer #(.enable("false")) multiplexer_8 (.in0(prev8), .in1(M8), .out(O8), .sel(or_1_out));
  or or_1 (or_1_out, M1, M2, M3, M4, M5, M6, M7, M8);
endmodule

module All_Blocks (
  input  [7:0] EVT,
  input  [31:0] NUMBER_1,
  input  [31:0] NUMBER_2,
  input  [31:0] NUMBER_3,
  input  [31:0] NUMBER_4,
  input  [31:0] NUMBER_5,
  input  [31:0] NUMBER_6,
  input  [31:0] NUMBER_7,
  input  [31:0] NUMBER_8,
  output O1,
  output O2,
  output O3,
  output O4,
  output O5,
  output O6,
  output O7,
  output O8
);

  wire B0_o1, B0_o2, B0_o3, B0_o4, B0_o5, B0_o6, B0_o7, B0_o8, B1_o1, B1_o2, B1_o3, B1_o4, B1_o5, B1_o6,
       B1_o7, B1_o8, B2_o1, B2_o2, B2_o3, B2_o4, B2_o5, B2_o6, B2_o7, B2_o8, B3_o1, B3_o2, B3_o3, B3_o4,
       B3_o5, B3_o6, B3_o7, B3_o8, B4_o1, B4_o2, B4_o3, B4_o4, B4_o5, B4_o6, B4_o7, B4_o8, B5_o1, B5_o2,
       B5_o3, B5_o4, B5_o5, B5_o6, B5_o7, B5_o8, B6_o1, B6_o2, B6_o3, B6_o4, B6_o5, B6_o6, B6_o7, B6_o8,
       B8_o1, B8_o2, B8_o3, B8_o4, B8_o5, B8_o6, B8_o7, B8_o8, B9_o1, B9_o2, B9_o3, B9_o4, B9_o5, B9_o6,
       B9_o7, B9_o8, B10_o1, B10_o2, B10_o3, B10_o4, B10_o5, B10_o6, B10_o7, B10_o8, B11_o1, B11_o2, B11_o3,
       B11_o4, B11_o5, B11_o6, B11_o7, B11_o8, B12_o1, B12_o2, B12_o3, B12_o4, B12_o5, B12_o6, B12_o7,
       B12_o8, B13_o1, B13_o2, B13_o3, B13_o4, B13_o5, B13_o6, B13_o7, B13_o8, B14_o1, B14_o2, B14_o3,
       B14_o4, B14_o5, B14_o6, B14_o7, B14_o8, B16_o1, B16_o2, B16_o3, B16_o4, B16_o5, B16_o6, B16_o7,
       B16_o8, B17_o1, B17_o2, B17_o3, B17_o4, B17_o5, B17_o6, B17_o7, B17_o8, B18_o1, B18_o2, B18_o3,
       B18_o4, B18_o5, B18_o6, B18_o7, B18_o8, B19_o1, B19_o2, B19_o3, B19_o4, B19_o5, B19_o6, B19_o7,
       B19_o8, B20_o1, B20_o2, B20_o3, B20_o4, B20_o5, B20_o6, B20_o7, B20_o8, B21_o1, B21_o2, B21_o3,
       B21_o4, B21_o5, B21_o6, B21_o7, B21_o8, B22_o1, B22_o2, B22_o3, B22_o4, B22_o5, B22_o6, B22_o7,
       B22_o8, B24_o1, B24_o2, B24_o3, B24_o4, B24_o5, B24_o6, B24_o7, B24_o8, B25_o1, B25_o2, B25_o3,
       B25_o4, B25_o5, B25_o6, B25_o7, B25_o8, B26_o1, B26_o2, B26_o3, B26_o4, B26_o5, B26_o6, B26_o7,
       B26_o8, B27_o1, B27_o2, B27_o3, B27_o4, B27_o5, B27_o6, B27_o7, B27_o8, B28_o1, B28_o2, B28_o3,
       B28_o4, B28_o5, B28_o6, B28_o7, B28_o8, B29_o1, B29_o2, B29_o3, B29_o4, B29_o5, B29_o6, B29_o7,
       B29_o8, B30_o1, B30_o2, B30_o3, B30_o4, B30_o5, B30_o6, B30_o7, B30_o8, N11, N12, N13, N14, N15, N16,
       N17, N18, N21, N22, N23, N24, N25, N26, N27, N28, N31, N32, N33, N34, N35, N36, N37, N38, not_1_out,
       not_2_out, not_3_out, not_4_out, not_5_out, not_6_out, not_7_out, not_8_out;

  not not_1 (not_1_out, NUMBER_1[31]);
  not not_2 (not_2_out, NUMBER_2[31]);
  not not_3 (not_3_out, NUMBER_3[31]);
  not not_4 (not_4_out, NUMBER_4[31]);
  not not_5 (not_5_out, NUMBER_5[31]);
  not not_6 (not_6_out, NUMBER_6[31]);
  not not_7 (not_7_out, NUMBER_7[31]);
  not not_8 (not_8_out, NUMBER_8[31]);
  BLOCK B0 (
    .prev1(EVT[0]), .MSB1(not_1_out), .prev2(EVT[1]), .MSB2(not_2_out), .prev3(EVT[2]), .MSB3(not_3_out),
    .prev4(EVT[3]), .MSB4(not_4_out), .prev5(EVT[4]), .MSB5(not_5_out), .prev6(EVT[5]), .MSB6(not_6_out),
    .prev7(EVT[6]), .MSB7(not_7_out), .prev8(EVT[7]), .MSB8(not_8_out), .O1(B0_o1), .O2(B0_o2), .O3(B0_o3),
    .O4(B0_o4), .O5(B0_o5), .O6(B0_o6), .O7(B0_o7), .O8(B0_o8));
  BLOCK B8 (
    .prev1(N11), .MSB1(NUMBER_1[23]), .prev2(N12), .MSB2(NUMBER_2[23]), .prev3(N13), .MSB3(NUMBER_3[23]),
    .prev4(N14), .MSB4(NUMBER_4[23]), .prev5(N15), .MSB5(NUMBER_5[23]), .prev6(N16), .MSB6(NUMBER_6[23]),
    .prev7(N17), .MSB7(NUMBER_7[23]), .prev8(N18), .MSB8(NUMBER_8[23]), .O1(B8_o1), .O2(B8_o2), .O3(B8_o3),
    .O4(B8_o4), .O5(B8_o5), .O6(B8_o6), .O7(B8_o7), .O8(B8_o8));
  BLOCK B16 (
    .prev1(N21), .MSB1(NUMBER_1[15]), .prev2(N22), .MSB2(NUMBER_2[15]), .prev3(N23), .MSB3(NUMBER_3[15]),
    .prev4(N24), .MSB4(NUMBER_4[15]), .prev5(N25), .MSB5(NUMBER_5[15]), .prev6(N26), .MSB6(NUMBER_6[15]),
    .prev7(N27), .MSB7(NUMBER_7[15]), .prev8(N28), .MSB8(NUMBER_8[15]), .O1(B16_o1), .O2(B16_o2),
    .O3(B16_o3), .O4(B16_o4), .O5(B16_o5), .O6(B16_o6), .O7(B16_o7), .O8(B16_o8));
  BLOCK B24 (
    .prev1(N31), .MSB1(NUMBER_1[7]), .prev2(N32), .MSB2(NUMBER_2[7]), .prev3(N33), .MSB3(NUMBER_3[7]),
    .prev4(N34), .MSB4(NUMBER_4[7]), .prev5(N35), .MSB5(NUMBER_5[7]), .prev6(N36), .MSB6(NUMBER_6[7]),
    .prev7(N37), .MSB7(NUMBER_7[7]), .prev8(N38), .MSB8(NUMBER_8[7]), .O1(B24_o1), .O2(B24_o2), .O3(B24_o3),
    .O4(B24_o4), .O5(B24_o5), .O6(B24_o6), .O7(B24_o7), .O8(B24_o8));
  BLOCK B1 (
    .prev1(B0_o1), .MSB1(NUMBER_1[30]), .prev2(B0_o2), .MSB2(NUMBER_2[30]), .prev3(B0_o3),
    .MSB3(NUMBER_3[30]), .prev4(B0_o4), .MSB4(NUMBER_4[30]), .prev5(B0_o5), .MSB5(NUMBER_5[30]),
    .prev6(B0_o6), .MSB6(NUMBER_6[30]), .prev7(B0_o7), .MSB7(NUMBER_7[30]), .prev8(B0_o8),
    .MSB8(NUMBER_8[30]), .O1(B1_o1), .O2(B1_o2), .O3(B1_o3), .O4(B1_o4), .O5(B1_o5), .O6(B1_o6), .O7(B1_o7),
    .O8(B1_o8));
  BLOCK B9 (
    .prev1(B8_o1), .MSB1(NUMBER_1[22]), .prev2(B8_o2), .MSB2(NUMBER_2[22]), .prev3(B8_o3),
    .MSB3(NUMBER_3[22]), .prev4(B8_o4), .MSB4(NUMBER_4[22]), .prev5(B8_o5), .MSB5(NUMBER_5[22]),
    .prev6(B8_o6), .MSB6(NUMBER_6[22]), .prev7(B8_o7), .MSB7(NUMBER_7[22]), .prev8(B8_o8),
    .MSB8(NUMBER_8[22]), .O1(B9_o1), .O2(B9_o2), .O3(B9_o3), .O4(B9_o4), .O5(B9_o5), .O6(B9_o6), .O7(B9_o7),
    .O8(B9_o8));
  BLOCK B17 (
    .prev1(B16_o1), .MSB1(NUMBER_1[14]), .prev2(B16_o2), .MSB2(NUMBER_2[14]), .prev3(B16_o3),
    .MSB3(NUMBER_3[14]), .prev4(B16_o4), .MSB4(NUMBER_4[14]), .prev5(B16_o5), .MSB5(NUMBER_5[14]),
    .prev6(B16_o6), .MSB6(NUMBER_6[14]), .prev7(B16_o7), .MSB7(NUMBER_7[14]), .prev8(B16_o8),
    .MSB8(NUMBER_8[14]), .O1(B17_o1), .O2(B17_o2), .O3(B17_o3), .O4(B17_o4), .O5(B17_o5), .O6(B17_o6),
    .O7(B17_o7), .O8(B17_o8));
  BLOCK B25 (
    .prev1(B24_o1), .MSB1(NUMBER_1[6]), .prev2(B24_o2), .MSB2(NUMBER_2[6]), .prev3(B24_o3),
    .MSB3(NUMBER_3[6]), .prev4(B24_o4), .MSB4(NUMBER_4[6]), .prev5(B24_o5), .MSB5(NUMBER_5[6]),
    .prev6(B24_o6), .MSB6(NUMBER_6[6]), .prev7(B24_o7), .MSB7(NUMBER_7[6]), .prev8(B24_o8),
    .MSB8(NUMBER_8[6]), .O1(B25_o1), .O2(B25_o2), .O3(B25_o3), .O4(B25_o4), .O5(B25_o5), .O6(B25_o6),
    .O7(B25_o7), .O8(B25_o8));
  BLOCK B2 (
    .prev1(B1_o1), .MSB1(NUMBER_1[29]), .prev2(B1_o2), .MSB2(NUMBER_2[29]), .prev3(B1_o3),
    .MSB3(NUMBER_3[29]), .prev4(B1_o4), .MSB4(NUMBER_4[29]), .prev5(B1_o5), .MSB5(NUMBER_5[29]),
    .prev6(B1_o6), .MSB6(NUMBER_6[29]), .prev7(B1_o7), .MSB7(NUMBER_7[29]), .prev8(B1_o8),
    .MSB8(NUMBER_8[29]), .O1(B2_o1), .O2(B2_o2), .O3(B2_o3), .O4(B2_o4), .O5(B2_o5), .O6(B2_o6), .O7(B2_o7),
    .O8(B2_o8));
  BLOCK B10 (
    .prev1(B9_o1), .MSB1(NUMBER_1[21]), .prev2(B9_o2), .MSB2(NUMBER_2[21]), .prev3(B9_o3),
    .MSB3(NUMBER_3[21]), .prev4(B9_o4), .MSB4(NUMBER_4[21]), .prev5(B9_o5), .MSB5(NUMBER_5[21]),
    .prev6(B9_o6), .MSB6(NUMBER_6[21]), .prev7(B9_o7), .MSB7(NUMBER_7[21]), .prev8(B9_o8),
    .MSB8(NUMBER_8[21]), .O1(B10_o1), .O2(B10_o2), .O3(B10_o3), .O4(B10_o4), .O5(B10_o5), .O6(B10_o6),
    .O7(B10_o7), .O8(B10_o8));
  BLOCK B18 (
    .prev1(B17_o1), .MSB1(NUMBER_1[13]), .prev2(B17_o2), .MSB2(NUMBER_2[13]), .prev3(B17_o3),
    .MSB3(NUMBER_3[13]), .prev4(B17_o4), .MSB4(NUMBER_4[13]), .prev5(B17_o5), .MSB5(NUMBER_5[13]),
    .prev6(B17_o6), .MSB6(NUMBER_6[13]), .prev7(B17_o7), .MSB7(NUMBER_7[13]), .prev8(B17_o8),
    .MSB8(NUMBER_8[13]), .O1(B18_o1), .O2(B18_o2), .O3(B18_o3), .O4(B18_o4), .O5(B18_o5), .O6(B18_o6),
    .O7(B18_o7), .O8(B18_o8));
  BLOCK B26 (
    .prev1(B25_o1), .MSB1(NUMBER_1[5]), .prev2(B25_o2), .MSB2(NUMBER_2[5]), .prev3(B25_o3),
    .MSB3(NUMBER_3[5]), .prev4(B25_o4), .MSB4(NUMBER_4[5]), .prev5(B25_o5), .MSB5(NUMBER_5[5]),
    .prev6(B25_o6), .MSB6(NUMBER_6[5]), .prev7(B25_o7), .MSB7(NUMBER_7[5]), .prev8(B25_o8),
    .MSB8(NUMBER_8[5]), .O1(B26_o1), .O2(B26_o2), .O3(B26_o3), .O4(B26_o4), .O5(B26_o5), .O6(B26_o6),
    .O7(B26_o7), .O8(B26_o8));
  BLOCK B3 (
    .prev1(B2_o1), .MSB1(NUMBER_1[28]), .prev2(B2_o2), .MSB2(NUMBER_2[28]), .prev3(B2_o3),
    .MSB3(NUMBER_3[28]), .prev4(B2_o4), .MSB4(NUMBER_4[28]), .prev5(B2_o5), .MSB5(NUMBER_5[28]),
    .prev6(B2_o6), .MSB6(NUMBER_6[28]), .prev7(B2_o7), .MSB7(NUMBER_7[28]), .prev8(B2_o8),
    .MSB8(NUMBER_8[28]), .O1(B3_o1), .O2(B3_o2), .O3(B3_o3), .O4(B3_o4), .O5(B3_o5), .O6(B3_o6), .O7(B3_o7),
    .O8(B3_o8));
  BLOCK B11 (
    .prev1(B10_o1), .MSB1(NUMBER_1[20]), .prev2(B10_o2), .MSB2(NUMBER_2[20]), .prev3(B10_o3),
    .MSB3(NUMBER_3[20]), .prev4(B10_o4), .MSB4(NUMBER_4[20]), .prev5(B10_o5), .MSB5(NUMBER_5[20]),
    .prev6(B10_o6), .MSB6(NUMBER_6[20]), .prev7(B10_o7), .MSB7(NUMBER_7[20]), .prev8(B10_o8),
    .MSB8(NUMBER_8[20]), .O1(B11_o1), .O2(B11_o2), .O3(B11_o3), .O4(B11_o4), .O5(B11_o5), .O6(B11_o6),
    .O7(B11_o7), .O8(B11_o8));
  BLOCK B19 (
    .prev1(B18_o1), .MSB1(NUMBER_1[12]), .prev2(B18_o2), .MSB2(NUMBER_2[12]), .prev3(B18_o3),
    .MSB3(NUMBER_3[12]), .prev4(B18_o4), .MSB4(NUMBER_4[12]), .prev5(B18_o5), .MSB5(NUMBER_5[12]),
    .prev6(B18_o6), .MSB6(NUMBER_6[12]), .prev7(B18_o7), .MSB7(NUMBER_7[12]), .prev8(B18_o8),
    .MSB8(NUMBER_8[12]), .O1(B19_o1), .O2(B19_o2), .O3(B19_o3), .O4(B19_o4), .O5(B19_o5), .O6(B19_o6),
    .O7(B19_o7), .O8(B19_o8));
  BLOCK B27 (
    .prev1(B26_o1), .MSB1(NUMBER_1[4]), .prev2(B26_o2), .MSB2(NUMBER_2[4]), .prev3(B26_o3),
    .MSB3(NUMBER_3[4]), .prev4(B26_o4), .MSB4(NUMBER_4[4]), .prev5(B26_o5), .MSB5(NUMBER_5[4]),
    .prev6(B26_o6), .MSB6(NUMBER_6[4]), .prev7(B26_o7), .MSB7(NUMBER_7[4]), .prev8(B26_o8),
    .MSB8(NUMBER_8[4]), .O1(B27_o1), .O2(B27_o2), .O3(B27_o3), .O4(B27_o4), .O5(B27_o5), .O6(B27_o6),
    .O7(B27_o7), .O8(B27_o8));
  BLOCK B4 (
    .prev1(B3_o1), .MSB1(NUMBER_1[27]), .prev2(B3_o2), .MSB2(NUMBER_2[27]), .prev3(B3_o3),
    .MSB3(NUMBER_3[27]), .prev4(B3_o4), .MSB4(NUMBER_4[27]), .prev5(B3_o5), .MSB5(NUMBER_5[27]),
    .prev6(B3_o6), .MSB6(NUMBER_6[27]), .prev7(B3_o7), .MSB7(NUMBER_7[27]), .prev8(B3_o8),
    .MSB8(NUMBER_8[27]), .O1(B4_o1), .O2(B4_o2), .O3(B4_o3), .O4(B4_o4), .O5(B4_o5), .O6(B4_o6), .O7(B4_o7),
    .O8(B4_o8));
  BLOCK B12 (
    .prev1(B11_o1), .MSB1(NUMBER_1[19]), .prev2(B11_o2), .MSB2(NUMBER_2[19]), .prev3(B11_o3),
    .MSB3(NUMBER_3[19]), .prev4(B11_o4), .MSB4(NUMBER_4[19]), .prev5(B11_o5), .MSB5(NUMBER_5[19]),
    .prev6(B11_o6), .MSB6(NUMBER_6[19]), .prev7(B11_o7), .MSB7(NUMBER_7[19]), .prev8(B11_o8),
    .MSB8(NUMBER_8[19]), .O1(B12_o1), .O2(B12_o2), .O3(B12_o3), .O4(B12_o4), .O5(B12_o5), .O6(B12_o6),
    .O7(B12_o7), .O8(B12_o8));
  BLOCK B20 (
    .prev1(B19_o1), .MSB1(NUMBER_1[11]), .prev2(B19_o2), .MSB2(NUMBER_2[11]), .prev3(B19_o3),
    .MSB3(NUMBER_3[11]), .prev4(B19_o4), .MSB4(NUMBER_4[11]), .prev5(B19_o5), .MSB5(NUMBER_5[11]),
    .prev6(B19_o6), .MSB6(NUMBER_6[11]), .prev7(B19_o7), .MSB7(NUMBER_7[11]), .prev8(B19_o8),
    .MSB8(NUMBER_8[11]), .O1(B20_o1), .O2(B20_o2), .O3(B20_o3), .O4(B20_o4), .O5(B20_o5), .O6(B20_o6),
    .O7(B20_o7), .O8(B20_o8));
  BLOCK B28 (
    .prev1(B27_o1), .MSB1(NUMBER_1[3]), .prev2(B27_o2), .MSB2(NUMBER_2[3]), .prev3(B27_o3),
    .MSB3(NUMBER_3[3]), .prev4(B27_o4), .MSB4(NUMBER_4[3]), .prev5(B27_o5), .MSB5(NUMBER_5[3]),
    .prev6(B27_o6), .MSB6(NUMBER_6[3]), .prev7(B27_o7), .MSB7(NUMBER_7[3]), .prev8(B27_o8),
    .MSB8(NUMBER_8[3]), .O1(B28_o1), .O2(B28_o2), .O3(B28_o3), .O4(B28_o4), .O5(B28_o5), .O6(B28_o6),
    .O7(B28_o7), .O8(B28_o8));
  BLOCK B5 (
    .prev1(B4_o1), .MSB1(NUMBER_1[26]), .prev2(B4_o2), .MSB2(NUMBER_2[26]), .prev3(B4_o3),
    .MSB3(NUMBER_3[26]), .prev4(B4_o4), .MSB4(NUMBER_4[26]), .prev5(B4_o5), .MSB5(NUMBER_5[26]),
    .prev6(B4_o6), .MSB6(NUMBER_6[26]), .prev7(B4_o7), .MSB7(NUMBER_7[26]), .prev8(B4_o8),
    .MSB8(NUMBER_8[26]), .O1(B5_o1), .O2(B5_o2), .O3(B5_o3), .O4(B5_o4), .O5(B5_o5), .O6(B5_o6), .O7(B5_o7),
    .O8(B5_o8));
  BLOCK B13 (
    .prev1(B12_o1), .MSB1(NUMBER_1[18]), .prev2(B12_o2), .MSB2(NUMBER_2[18]), .prev3(B12_o3),
    .MSB3(NUMBER_3[18]), .prev4(B12_o4), .MSB4(NUMBER_4[18]), .prev5(B12_o5), .MSB5(NUMBER_5[18]),
    .prev6(B12_o6), .MSB6(NUMBER_6[18]), .prev7(B12_o7), .MSB7(NUMBER_7[18]), .prev8(B12_o8),
    .MSB8(NUMBER_8[18]), .O1(B13_o1), .O2(B13_o2), .O3(B13_o3), .O4(B13_o4), .O5(B13_o5), .O6(B13_o6),
    .O7(B13_o7), .O8(B13_o8));
  BLOCK B21 (
    .prev1(B20_o1), .MSB1(NUMBER_1[10]), .prev2(B20_o2), .MSB2(NUMBER_2[10]), .prev3(B20_o3),
    .MSB3(NUMBER_3[10]), .prev4(B20_o4), .MSB4(NUMBER_4[10]), .prev5(B20_o5), .MSB5(NUMBER_5[10]),
    .prev6(B20_o6), .MSB6(NUMBER_6[10]), .prev7(B20_o7), .MSB7(NUMBER_7[10]), .prev8(B20_o8),
    .MSB8(NUMBER_8[10]), .O1(B21_o1), .O2(B21_o2), .O3(B21_o3), .O4(B21_o4), .O5(B21_o5), .O6(B21_o6),
    .O7(B21_o7), .O8(B21_o8));
  BLOCK B29 (
    .prev1(B28_o1), .MSB1(NUMBER_1[2]), .prev2(B28_o2), .MSB2(NUMBER_2[2]), .prev3(B28_o3),
    .MSB3(NUMBER_3[2]), .prev4(B28_o4), .MSB4(NUMBER_4[2]), .prev5(B28_o5), .MSB5(NUMBER_5[2]),
    .prev6(B28_o6), .MSB6(NUMBER_6[2]), .prev7(B28_o7), .MSB7(NUMBER_7[2]), .prev8(B28_o8),
    .MSB8(NUMBER_8[2]), .O1(B29_o1), .O2(B29_o2), .O3(B29_o3), .O4(B29_o4), .O5(B29_o5), .O6(B29_o6),
    .O7(B29_o7), .O8(B29_o8));
  BLOCK B6 (
    .prev1(B5_o1), .MSB1(NUMBER_1[25]), .prev2(B5_o2), .MSB2(NUMBER_2[25]), .prev3(B5_o3),
    .MSB3(NUMBER_3[25]), .prev4(B5_o4), .MSB4(NUMBER_4[25]), .prev5(B5_o5), .MSB5(NUMBER_5[25]),
    .prev6(B5_o6), .MSB6(NUMBER_6[25]), .prev7(B5_o7), .MSB7(NUMBER_7[25]), .prev8(B5_o8),
    .MSB8(NUMBER_8[25]), .O1(B6_o1), .O2(B6_o2), .O3(B6_o3), .O4(B6_o4), .O5(B6_o5), .O6(B6_o6), .O7(B6_o7),
    .O8(B6_o8));
  BLOCK B14 (
    .prev1(B13_o1), .MSB1(NUMBER_1[17]), .prev2(B13_o2), .MSB2(NUMBER_2[17]), .prev3(B13_o3),
    .MSB3(NUMBER_3[17]), .prev4(B13_o4), .MSB4(NUMBER_4[17]), .prev5(B13_o5), .MSB5(NUMBER_5[17]),
    .prev6(B13_o6), .MSB6(NUMBER_6[17]), .prev7(B13_o7), .MSB7(NUMBER_7[17]), .prev8(B13_o8),
    .MSB8(NUMBER_8[17]), .O1(B14_o1), .O2(B14_o2), .O3(B14_o3), .O4(B14_o4), .O5(B14_o5), .O6(B14_o6),
    .O7(B14_o7), .O8(B14_o8));
  BLOCK B22 (
    .prev1(B21_o1), .MSB1(NUMBER_1[9]), .prev2(B21_o2), .MSB2(NUMBER_2[9]), .prev3(B21_o3),
    .MSB3(NUMBER_3[9]), .prev4(B21_o4), .MSB4(NUMBER_4[9]), .prev5(B21_o5), .MSB5(NUMBER_5[9]),
    .prev6(B21_o6), .MSB6(NUMBER_6[9]), .prev7(B21_o7), .MSB7(NUMBER_7[9]), .prev8(B21_o8),
    .MSB8(NUMBER_8[9]), .O1(B22_o1), .O2(B22_o2), .O3(B22_o3), .O4(B22_o4), .O5(B22_o5), .O6(B22_o6),
    .O7(B22_o7), .O8(B22_o8));
  BLOCK B30 (
    .prev1(B29_o1), .MSB1(NUMBER_1[1]), .prev2(B29_o2), .MSB2(NUMBER_2[1]), .prev3(B29_o3),
    .MSB3(NUMBER_3[1]), .prev4(B29_o4), .MSB4(NUMBER_4[1]), .prev5(B29_o5), .MSB5(NUMBER_5[1]),
    .prev6(B29_o6), .MSB6(NUMBER_6[1]), .prev7(B29_o7), .MSB7(NUMBER_7[1]), .prev8(B29_o8),
    .MSB8(NUMBER_8[1]), .O1(B30_o1), .O2(B30_o2), .O3(B30_o3), .O4(B30_o4), .O5(B30_o5), .O6(B30_o6),
    .O7(B30_o7), .O8(B30_o8));
  BLOCK B7 (
    .prev1(B6_o1), .MSB1(NUMBER_1[24]), .prev2(B6_o2), .MSB2(NUMBER_2[24]), .prev3(B6_o3),
    .MSB3(NUMBER_3[24]), .prev4(B6_o4), .MSB4(NUMBER_4[24]), .prev5(B6_o5), .MSB5(NUMBER_5[24]),
    .prev6(B6_o6), .MSB6(NUMBER_6[24]), .prev7(B6_o7), .MSB7(NUMBER_7[24]), .prev8(B6_o8),
    .MSB8(NUMBER_8[24]), .O1(N11), .O2(N12), .O3(N13), .O4(N14), .O5(N15), .O6(N16), .O7(N17), .O8(N18));
  BLOCK B15 (
    .prev1(B14_o1), .MSB1(NUMBER_1[16]), .prev2(B14_o2), .MSB2(NUMBER_2[16]), .prev3(B14_o3),
    .MSB3(NUMBER_3[16]), .prev4(B14_o4), .MSB4(NUMBER_4[16]), .prev5(B14_o5), .MSB5(NUMBER_5[16]),
    .prev6(B14_o6), .MSB6(NUMBER_6[16]), .prev7(B14_o7), .MSB7(NUMBER_7[16]), .prev8(B14_o8),
    .MSB8(NUMBER_8[16]), .O1(N21), .O2(N22), .O3(N23), .O4(N24), .O5(N25), .O6(N26), .O7(N27), .O8(N28));
  BLOCK B23 (
    .prev1(B22_o1), .MSB1(NUMBER_1[8]), .prev2(B22_o2), .MSB2(NUMBER_2[8]), .prev3(B22_o3),
    .MSB3(NUMBER_3[8]), .prev4(B22_o4), .MSB4(NUMBER_4[8]), .prev5(B22_o5), .MSB5(NUMBER_5[8]),
    .prev6(B22_o6), .MSB6(NUMBER_6[8]), .prev7(B22_o7), .MSB7(NUMBER_7[8]), .prev8(B22_o8),
    .MSB8(NUMBER_8[8]), .O1(N31), .O2(N32), .O3(N33), .O4(N34), .O5(N35), .O6(N36), .O7(N37), .O8(N38));
  BLOCK B31 (
    .prev1(B30_o1), .MSB1(NUMBER_1[0]), .prev2(B30_o2), .MSB2(NUMBER_2[0]), .prev3(B30_o3),
    .MSB3(NUMBER_3[0]), .prev4(B30_o4), .MSB4(NUMBER_4[0]), .prev5(B30_o5), .MSB5(NUMBER_5[0]),
    .prev6(B30_o6), .MSB6(NUMBER_6[0]), .prev7(B30_o7), .MSB7(NUMBER_7[0]), .prev8(B30_o8),
    .MSB8(NUMBER_8[0]), .O1(O1), .O2(O2), .O3(O3), .O4(O4), .O5(O5), .O6(O6), .O7(O7), .O8(O8));

  // Other names for the same wires on the sheet: D131 = NUMBER_1[0]; D130 = NUMBER_1[1]; D129 = NUMBER_1[2];
  //   D128 = NUMBER_1[3]; D127 = NUMBER_1[4]; D126 = NUMBER_1[5]; D125 = NUMBER_1[6]; D124 = NUMBER_1[7];
  //   D123 = NUMBER_1[8]; D122 = NUMBER_1[9]; D121 = NUMBER_1[10]; D120 = NUMBER_1[11]; D119 = NUMBER_1[12];
  //   D118 = NUMBER_1[13]; D117 = NUMBER_1[14]; D116 = NUMBER_1[15]; D115 = NUMBER_1[16]; D114 = NUMBER_1[17];
  //   D113 = NUMBER_1[18]; D112 = NUMBER_1[19]; D111 = NUMBER_1[20]; D110 = NUMBER_1[21]; D19 = NUMBER_1[22];
  //   D18 = NUMBER_1[23]; D17 = NUMBER_1[24]; D16 = NUMBER_1[25]; D15 = NUMBER_1[26]; D14 = NUMBER_1[27];
  //   D13 = NUMBER_1[28]; D12 = NUMBER_1[29]; D11 = NUMBER_1[30]; D10 = NUMBER_1[31]; D231 = NUMBER_2[0];
  //   D230 = NUMBER_2[1]; D229 = NUMBER_2[2]; D228 = NUMBER_2[3]; D227 = NUMBER_2[4]; D226 = NUMBER_2[5];
  //   D225 = NUMBER_2[6]; D224 = NUMBER_2[7]; D223 = NUMBER_2[8]; D222 = NUMBER_2[9]; D221 = NUMBER_2[10];
  //   D220 = NUMBER_2[11]; D219 = NUMBER_2[12]; D218 = NUMBER_2[13]; D217 = NUMBER_2[14]; D216 = NUMBER_2[15];
  //   D215 = NUMBER_2[16]; D214 = NUMBER_2[17]; D213 = NUMBER_2[18]; D212 = NUMBER_2[19]; D211 = NUMBER_2[20];
  //   D210 = NUMBER_2[21]; D29 = NUMBER_2[22]; D28 = NUMBER_2[23]; D27 = NUMBER_2[24]; D26 = NUMBER_2[25];
  //   D25 = NUMBER_2[26]; D24 = NUMBER_2[27]; D23 = NUMBER_2[28]; D22 = NUMBER_2[29]; D21 = NUMBER_2[30];
  //   D20 = NUMBER_2[31]; D331 = NUMBER_3[0]; D330 = NUMBER_3[1]; D329 = NUMBER_3[2]; D328 = NUMBER_3[3];
  //   D327 = NUMBER_3[4]; D326 = NUMBER_3[5]; D325 = NUMBER_3[6]; D324 = NUMBER_3[7]; D323 = NUMBER_3[8];
  //   D322 = NUMBER_3[9]; D321 = NUMBER_3[10]; D320 = NUMBER_3[11]; D319 = NUMBER_3[12]; D318 = NUMBER_3[13];
  //   D317 = NUMBER_3[14]; D316 = NUMBER_3[15]; D315 = NUMBER_3[16]; D314 = NUMBER_3[17]; D313 = NUMBER_3[18];
  //   D312 = NUMBER_3[19]; D311 = NUMBER_3[20]; D310 = NUMBER_3[21]; D39 = NUMBER_3[22]; D38 = NUMBER_3[23];
  //   D37 = NUMBER_3[24]; D36 = NUMBER_3[25]; D35 = NUMBER_3[26]; D34 = NUMBER_3[27]; D33 = NUMBER_3[28];
  //   D32 = NUMBER_3[29]; D31 = NUMBER_3[30]; D30 = NUMBER_3[31]; D431 = NUMBER_4[0]; D430 = NUMBER_4[1];
  //   D429 = NUMBER_4[2]; D428 = NUMBER_4[3]; D427 = NUMBER_4[4]; D426 = NUMBER_4[5]; D425 = NUMBER_4[6];
  //   D424 = NUMBER_4[7]; D423 = NUMBER_4[8]; D422 = NUMBER_4[9]; D421 = NUMBER_4[10]; D420 = NUMBER_4[11];
  //   D419 = NUMBER_4[12]; D418 = NUMBER_4[13]; D417 = NUMBER_4[14]; D416 = NUMBER_4[15]; D415 = NUMBER_4[16];
  //   D414 = NUMBER_4[17]; D413 = NUMBER_4[18]; D412 = NUMBER_4[19]; D411 = NUMBER_4[20]; D410 = NUMBER_4[21];
  //   D49 = NUMBER_4[22]; D48 = NUMBER_4[23]; D47 = NUMBER_4[24]; D46 = NUMBER_4[25]; D45 = NUMBER_4[26];
  //   D44 = NUMBER_4[27]; D43 = NUMBER_4[28]; D42 = NUMBER_4[29]; D41 = NUMBER_4[30]; D40 = NUMBER_4[31];
  //   D531 = NUMBER_5[0]; D530 = NUMBER_5[1]; D529 = NUMBER_5[2]; D528 = NUMBER_5[3]; D527 = NUMBER_5[4];
  //   D526 = NUMBER_5[5]; D525 = NUMBER_5[6]; D524 = NUMBER_5[7]; D523 = NUMBER_5[8]; D522 = NUMBER_5[9];
  //   D521 = NUMBER_5[10]; D520 = NUMBER_5[11]; D519 = NUMBER_5[12]; D518 = NUMBER_5[13]; D517 = NUMBER_5[14];
  //   D516 = NUMBER_5[15]; D515 = NUMBER_5[16]; D514 = NUMBER_5[17]; D513 = NUMBER_5[18]; D512 = NUMBER_5[19];
  //   D511 = NUMBER_5[20]; D510 = NUMBER_5[21]; D59 = NUMBER_5[22]; D58 = NUMBER_5[23]; D57 = NUMBER_5[24];
  //   D56 = NUMBER_5[25]; D55 = NUMBER_5[26]; D54 = NUMBER_5[27]; D53 = NUMBER_5[28]; D52 = NUMBER_5[29];
  //   D51 = NUMBER_5[30]; D50 = NUMBER_5[31]; D631 = NUMBER_6[0]; D630 = NUMBER_6[1]; D629 = NUMBER_6[2];
  //   D628 = NUMBER_6[3]; D627 = NUMBER_6[4]; D626 = NUMBER_6[5]; D625 = NUMBER_6[6]; D624 = NUMBER_6[7];
  //   D623 = NUMBER_6[8]; D622 = NUMBER_6[9]; D621 = NUMBER_6[10]; D620 = NUMBER_6[11]; D619 = NUMBER_6[12];
  //   D618 = NUMBER_6[13]; D617 = NUMBER_6[14]; D616 = NUMBER_6[15]; D615 = NUMBER_6[16]; D614 = NUMBER_6[17];
  //   D613 = NUMBER_6[18]; D612 = NUMBER_6[19]; D611 = NUMBER_6[20]; D610 = NUMBER_6[21]; D69 = NUMBER_6[22];
  //   D68 = NUMBER_6[23]; D67 = NUMBER_6[24]; D66 = NUMBER_6[25]; D65 = NUMBER_6[26]; D64 = NUMBER_6[27];
  //   D63 = NUMBER_6[28]; D62 = NUMBER_6[29]; D61 = NUMBER_6[30]; D60 = NUMBER_6[31]; D731 = NUMBER_7[0];
  //   D730 = NUMBER_7[1]; D729 = NUMBER_7[2]; D728 = NUMBER_7[3]; D727 = NUMBER_7[4]; D726 = NUMBER_7[5];
  //   D725 = NUMBER_7[6]; D724 = NUMBER_7[7]; D723 = NUMBER_7[8]; D722 = NUMBER_7[9]; D721 = NUMBER_7[10];
  //   D720 = NUMBER_7[11]; D719 = NUMBER_7[12]; D718 = NUMBER_7[13]; D717 = NUMBER_7[14]; D716 = NUMBER_7[15];
  //   D715 = NUMBER_7[16]; D714 = NUMBER_7[17]; D713 = NUMBER_7[18]; D712 = NUMBER_7[19]; D711 = NUMBER_7[20];
  //   D710 = NUMBER_7[21]; D79 = NUMBER_7[22]; D78 = NUMBER_7[23]; D77 = NUMBER_7[24]; D76 = NUMBER_7[25];
  //   D75 = NUMBER_7[26]; D74 = NUMBER_7[27]; D73 = NUMBER_7[28]; D72 = NUMBER_7[29]; D71 = NUMBER_7[30];
  //   D70 = NUMBER_7[31]; D831 = NUMBER_8[0]; D830 = NUMBER_8[1]; D829 = NUMBER_8[2]; D828 = NUMBER_8[3];
  //   D827 = NUMBER_8[4]; D826 = NUMBER_8[5]; D825 = NUMBER_8[6]; D824 = NUMBER_8[7]; D823 = NUMBER_8[8];
  //   D822 = NUMBER_8[9]; D821 = NUMBER_8[10]; D820 = NUMBER_8[11]; D819 = NUMBER_8[12]; D818 = NUMBER_8[13];
  //   D817 = NUMBER_8[14]; D816 = NUMBER_8[15]; D815 = NUMBER_8[16]; D814 = NUMBER_8[17]; D813 = NUMBER_8[18];
  //   D812 = NUMBER_8[19]; D811 = NUMBER_8[20]; D810 = NUMBER_8[21]; D89 = NUMBER_8[22]; D88 = NUMBER_8[23];
  //   D87 = NUMBER_8[24]; D86 = NUMBER_8[25]; D85 = NUMBER_8[26]; D84 = NUMBER_8[27]; D83 = NUMBER_8[28];
  //   D82 = NUMBER_8[29]; D81 = NUMBER_8[30]; D80 = NUMBER_8[31]
endmodule

module EVT_Update_Unit (
  input  [7:0] EVT,
  input  [7:0] Largest_Address_finder,
  input  Clock,
  output [7:0] Ouput_EVT
);

  wire and_1_out, and_2_out, and_3_out, and_4_out, and_5_out, and_6_out, and_7_out, and_8_out, not_1_out,
       not_2_out, not_3_out, not_4_out, not_5_out, not_6_out, not_7_out, not_8_out;

  not not_1 (not_1_out, Largest_Address_finder[0]);
  not not_2 (not_2_out, Largest_Address_finder[1]);
  not not_3 (not_3_out, Largest_Address_finder[2]);
  not not_4 (not_4_out, Largest_Address_finder[4]);
  not not_5 (not_5_out, Largest_Address_finder[5]);
  not not_6 (not_6_out, Largest_Address_finder[6]);
  not not_7 (not_7_out, Largest_Address_finder[7]);
  and and_1 (and_1_out, EVT[0], not_1_out);
  and and_2 (and_2_out, not_2_out, EVT[1]);
  and and_3 (and_3_out, not_3_out, EVT[2]);
  not not_8 (not_8_out, Largest_Address_finder[3]);
  and and_4 (and_4_out, not_8_out, EVT[3]);
  and and_5 (and_5_out, not_4_out, EVT[4]);
  and and_6 (and_6_out, not_5_out, EVT[5]);
  and and_7 (and_7_out, not_6_out, EVT[6]);
  and and_8 (and_8_out, not_7_out, EVT[7]);
  D_Flip_Flop BIT0 (.clk(Clock), .D(and_1_out), .Q(Ouput_EVT[0]));  // open: Qn, preset, en, reset
  D_Flip_Flop BIT1 (.clk(Clock), .D(and_2_out), .Q(Ouput_EVT[1]));  // open: Qn, preset, en, reset
  D_Flip_Flop BIT2 (.clk(Clock), .D(and_3_out), .Q(Ouput_EVT[2]));  // open: Qn, preset, en, reset
  D_Flip_Flop BIT3 (.clk(Clock), .D(and_4_out), .Q(Ouput_EVT[3]));  // open: Qn, preset, en, reset
  D_Flip_Flop BIT4 (.clk(Clock), .D(and_5_out), .Q(Ouput_EVT[4]));  // open: Qn, preset, en, reset
  D_Flip_Flop BIT5 (.clk(Clock), .D(and_6_out), .Q(Ouput_EVT[5]));  // open: Qn, preset, en, reset
  D_Flip_Flop BIT5_2 (.clk(Clock), .D(and_7_out), .Q(Ouput_EVT[6]));  // open: Qn, preset, en, reset
  D_Flip_Flop BIT6 (.clk(Clock), .D(and_8_out), .Q(Ouput_EVT[7]));  // open: Qn, preset, en, reset
endmodule

module Hardware_Sorter (
  input  [31:0] num1,
  input  [31:0] num2,
  input  Control,
  input  [31:0] num3,
  input  CLR,
  input  [31:0] num4,
  input  [31:0] num5,
  input  CLK_EVT,
  input  [31:0] num6,
  input  [31:0] num7,
  input  [31:0] num8,
  output [2:0] LE_address
);

  wire [7:0] all_blocks_1_o1, EVT_q, EVT_Update_Unit_ouput_evt, multiplexer_1_out;

  All_Blocks all_blocks_1 (
    .NUMBER_1(num1), .NUMBER_2(num2), .NUMBER_3(num3), .NUMBER_4(num4), .NUMBER_5(num5), .NUMBER_6(num6),
    .NUMBER_7(num7), .NUMBER_8(num8), .EVT(EVT_q), .O1(all_blocks_1_o1[0]), .O2(all_blocks_1_o1[1]),
    .O3(all_blocks_1_o1[2]), .O4(all_blocks_1_o1[3]), .O5(all_blocks_1_o1[4]), .O6(all_blocks_1_o1[5]),
    .O7(all_blocks_1_o1[6]), .O8(all_blocks_1_o1[7]));
  Multiplexer #(.width(8), .enable("false")) multiplexer_1 (
    .in0(EVT_Update_Unit_ouput_evt), .in1({8{1'b1}}), .out(multiplexer_1_out), .sel(Control));
  Largest_element_detector largest_element_detector_1 (
    .Input_from_terminal_block(all_blocks_1_o1), .LE_adress(LE_address));
  Register EVT (.D(multiplexer_1_out), .en(1'b1), .Q(EVT_q), .clk(CLK_EVT), .clr(CLR));
  EVT_Update_Unit EVT_Update_Unit (
    .EVT(EVT_q), .Largest_Address_finder(all_blocks_1_o1), .Ouput_EVT(EVT_Update_Unit_ouput_evt),
    .Clock(CLK_EVT));
endmodule

module Largest_element_detector (
  input  [7:0] Input_from_terminal_block,
  output [2:0] LE_adress
);

  wire and_1_out, and_2_out, and_3_out, and_4_out, and_5_out, and_6_out, and_7_out, not_1_out, not_2_out,
       not_3_out, not_4_out, not_5_out, not_6_out, not_7_out, or_1_out, or_2_out, or_3_out, or_4_out,
       or_5_out, or_6_out;

  not not_1 (not_1_out, Input_from_terminal_block[0]);
  or or_1 (or_1_out, Input_from_terminal_block[0], Input_from_terminal_block[1]);
  not not_2 (not_2_out, or_1_out);
  not not_3 (not_3_out, or_2_out);
  or or_2 (or_2_out, Input_from_terminal_block[0], Input_from_terminal_block[1], Input_from_terminal_block[2]);
  not not_4 (not_4_out, or_3_out);
  or or_3 (or_3_out, Input_from_terminal_block[0], Input_from_terminal_block[1], Input_from_terminal_block[2], Input_from_terminal_block[3]);
  not not_5 (not_5_out, or_4_out);
  or or_4 (or_4_out, Input_from_terminal_block[0], Input_from_terminal_block[1], Input_from_terminal_block[2], Input_from_terminal_block[3], Input_from_terminal_block[4]);
  not not_6 (not_6_out, or_5_out);
  or or_5 (or_5_out, Input_from_terminal_block[0], Input_from_terminal_block[1], Input_from_terminal_block[2], Input_from_terminal_block[3], Input_from_terminal_block[4], Input_from_terminal_block[5]);
  not not_7 (not_7_out, or_6_out);
  or or_6 (or_6_out, Input_from_terminal_block[0], Input_from_terminal_block[1], Input_from_terminal_block[2], Input_from_terminal_block[3], Input_from_terminal_block[4], Input_from_terminal_block[5], Input_from_terminal_block[6]);
  and and_1 (and_1_out, not_1_out, Input_from_terminal_block[1]);
  and and_2 (and_2_out, not_2_out, Input_from_terminal_block[2]);
  and and_3 (and_3_out, not_3_out, Input_from_terminal_block[3]);
  and and_4 (and_4_out, not_4_out, Input_from_terminal_block[4]);
  and and_5 (and_5_out, not_5_out, Input_from_terminal_block[5]);
  and and_6 (and_6_out, not_6_out, Input_from_terminal_block[6]);
  and and_7 (and_7_out, not_7_out, Input_from_terminal_block[7]);
  Priority_Encoder priority_encoder_1 (
    .in0(Input_from_terminal_block[0]), .in1(and_1_out), .in2(and_2_out), .in3(and_3_out), .in4(and_4_out),
    .in5(and_5_out), .in6(and_6_out), .in7(and_7_out), .out(LE_adress), .en_in(1'b1));  // open: gs, en_out
endmodule

module Unsorted_RF (
  input  [2:0] WriteRegister,
  input  [31:0] Write_Data,
  input  CLK,
  input  clr,
  output [31:0] Reg_out_0,
  output [31:0] Reg_out_2,
  output [31:0] Reg_out_4,
  output [31:0] Reg_out_6,
  output [31:0] Reg_out_1,
  output [31:0] Reg_out_3,
  output [31:0] Reg_out_5,
  output [31:0] Reg_out_7
);

  wire and_1_out, and_2_out, and_3_out, and_4_out, and_5_out, and_6_out, and_7_out, and_8_out,
       decoder_1_out0, decoder_1_out1, decoder_1_out2, decoder_1_out3, decoder_1_out4, decoder_1_out5,
       decoder_1_out6, decoder_1_out7;

  Decoder #(.select(3), .enable("false")) decoder_1 (
    .out0(decoder_1_out0), .out1(decoder_1_out1), .out2(decoder_1_out2), .out3(decoder_1_out3),
    .out4(decoder_1_out4), .out5(decoder_1_out5), .out6(decoder_1_out6), .out7(decoder_1_out7),
    .sel(WriteRegister));
  and and_1 (and_1_out, decoder_1_out0, 1'b1);
  and and_2 (and_2_out, decoder_1_out1, 1'b1);
  and and_3 (and_3_out, decoder_1_out2, 1'b1);
  and and_4 (and_4_out, decoder_1_out3, 1'b1);
  and and_5 (and_5_out, decoder_1_out4, 1'b1);
  and and_6 (and_6_out, decoder_1_out5, 1'b1);
  and and_7 (and_7_out, decoder_1_out6, 1'b1);
  and and_8 (and_8_out, decoder_1_out7, 1'b1);
  Register #(.width(32)) register_1 (.D(Write_Data), .en(and_1_out), .Q(Reg_out_0), .clk(CLK), .clr(clr));
  Register #(.width(32)) register_2 (.D(Write_Data), .en(and_2_out), .Q(Reg_out_1), .clk(CLK), .clr(clr));
  Register #(.width(32)) register_3 (.D(Write_Data), .en(and_3_out), .Q(Reg_out_2), .clk(CLK), .clr(clr));
  Register #(.width(32)) register_4 (.D(Write_Data), .en(and_4_out), .Q(Reg_out_3), .clk(CLK), .clr(clr));
  Register #(.width(32)) register_5 (.D(Write_Data), .en(and_5_out), .Q(Reg_out_4), .clk(CLK), .clr(clr));
  Register #(.width(32)) register_6 (.D(Write_Data), .en(and_6_out), .Q(Reg_out_5), .clk(CLK), .clr(clr));
  Register #(.width(32)) register_7 (.D(Write_Data), .en(and_7_out), .Q(Reg_out_6), .clk(CLK), .clr(clr));
  Register #(.width(32)) register_8 (.D(Write_Data), .en(and_8_out), .Q(Reg_out_7), .clk(CLK), .clr(clr));

  // Notes on the sheet:
  //   Write Bus
  //   R0
  //   R1
  //   R2
  //   R3
  //   R4
  //   R5
  //   R6
  //   R7
endmodule

module CTR (
  input  [2:0] changebit,
  input  CLK,
  input  CLR,
  output [2:0] OUTPUT
);

  wire [2:0] adder_1_out;

  Register #(.width(3)) register_1 (.D(adder_1_out), .en(1'b1), .Q(OUTPUT), .clk(CLK), .clr(CLR));
  Adder #(.width(3)) adder_1 (.a(changebit), .b(OUTPUT), .out(adder_1_out));  // open: cin, cout
endmodule

// Output_reader
module MUX_OUT (
  input  [31:0] Number_1,
  input  [31:0] Number_2,
  input  [31:0] Number_3,
  input  [31:0] Number_4,
  input  [2:0] I_P,
  input  [31:0] Number_5,
  input  [31:0] Number_6,
  input  [31:0] Number_7,
  input  [31:0] Number_8,
  output [31:0] OUT
);

  Multiplexer #(.select(3), .width(32), .enable("false")) multiplexer_1 (
    .in0(Number_1), .in1(Number_2), .in2(Number_3), .in3(Number_4), .in4(Number_5), .in5(Number_6),
    .in6(Number_7), .in7(Number_8), .out(OUT), .sel(I_P));
endmodule

// Output_Writer
module Sorted_RF (
  input  [2:0] WriteRegister,
  input  [31:0] Write_Data,
  input  Clock,
  input  clr,
  output [31:0] Reg_out_0,
  output [31:0] Reg_out_1,
  output [31:0] Reg_out_2,
  output [31:0] Reg_out_3,
  output [31:0] Reg_out_4,
  output [31:0] Reg_out_5,
  output [31:0] Reg_out_6,
  output [31:0] Reg_out_7
);

  wire decoder_1_out0, decoder_1_out1, decoder_1_out2, decoder_1_out3, decoder_1_out4, decoder_1_out5,
       decoder_1_out6, decoder_1_out7;

  Decoder #(.select(3), .enable("false")) decoder_1 (
    .out0(decoder_1_out0), .out1(decoder_1_out1), .out2(decoder_1_out2), .out3(decoder_1_out3),
    .out4(decoder_1_out4), .out5(decoder_1_out5), .out6(decoder_1_out6), .out7(decoder_1_out7),
    .sel(WriteRegister));
  Register #(.width(32)) register_1 (.D(Write_Data), .en(decoder_1_out0), .Q(Reg_out_0), .clk(Clock), .clr(clr));
  Register #(.width(32)) register_2 (.D(Write_Data), .en(decoder_1_out1), .Q(Reg_out_1), .clk(Clock), .clr(clr));
  Register #(.width(32)) register_3 (.D(Write_Data), .en(decoder_1_out2), .Q(Reg_out_2), .clk(Clock), .clr(clr));
  Register #(.width(32)) register_4 (.D(Write_Data), .en(decoder_1_out3), .Q(Reg_out_3), .clk(Clock), .clr(clr));
  Register #(.width(32)) register_5 (.D(Write_Data), .en(decoder_1_out4), .Q(Reg_out_4), .clk(Clock), .clr(clr));
  Register #(.width(32)) register_6 (.D(Write_Data), .en(decoder_1_out5), .Q(Reg_out_5), .clk(Clock), .clr(clr));
  Register #(.width(32)) register_7 (.D(Write_Data), .en(decoder_1_out6), .Q(Reg_out_6), .clk(Clock), .clr(clr));
  Register #(.width(32)) register_8 (.D(Write_Data), .en(decoder_1_out7), .Q(Reg_out_7), .clk(Clock), .clr(clr));

  // Notes on the sheet:
  //   Write Bus
  //   R0
  //   R1
  //   R2
  //   R3
  //   R4
  //   R5
  //   R6
  //   R7
endmodule

module Complete_Engine (
  input  [31:0] Number_1,
  input  [31:0] Number_2,
  input  [31:0] Number_3,
  input  [31:0] Number_4,
  input  [31:0] Number_5,
  input  [31:0] Number_6,
  input  [31:0] Number_7,
  input  [31:0] Number_8,
  input  Clear,
  input  Clock,
  output [31:0] out_11,
  output [31:0] out_12,
  output [31:0] out_13,
  output [31:0] out_14,
  output [31:0] out_15,
  output [31:0] out_16,
  output [31:0] out_17,
  output [31:0] out_18,
  output [31:0] F1,
  output [31:0] F2,
  output [31:0] F3,
  output [31:0] F4,
  output [31:0] F5,
  output [31:0] F6,
  output [31:0] F7,
  output [31:0] F8
);

  wire CLK, CLKK, or_1_out;
  wire [1:0] rom_1_data;
  wire [2:0] Cur, Curr, HS_le_address;
  wire [7:0] adder_1_out, register_1_q;
  wire [31:0] multiplexer_1_out, mux_out_1_out;

  Multiplexer #(.select(3), .width(32), .enable("false")) multiplexer_1 (
    .in0(Number_1), .in1(Number_2), .in2(Number_3), .in3(Number_4), .in4(Number_5), .in5(Number_6),
    .in6(Number_7), .in7(Number_8), .out(multiplexer_1_out), .sel(Curr));
  Register register_1 (.D(adder_1_out), .Q(register_1_q), .clk(Clock), .clr(Clear));  // open: en
  CTR ctr_1 (.changebit(3'b001), .CLK(CLKK), .CLR(Clear), .OUTPUT(Curr));
  Unsorted_RF unsorted_rf_1 (
    .Write_Data(multiplexer_1_out), .Reg_out_0(out_11), .Reg_out_2(out_13), .Reg_out_1(out_12),
    .Reg_out_4(out_15), .Reg_out_3(out_14), .Reg_out_6(out_17), .Reg_out_5(out_16), .Reg_out_7(out_18),
    .WriteRegister(Curr), .CLK(CLKK), .clr(Clear));
  Adder adder_1 (.a(8'h1), .b(register_1_q), .out(adder_1_out));  // open: cin, cout
  CTR ctr_2 (.changebit(3'b001), .CLK(CLK), .CLR(Clear), .OUTPUT(Cur));
  MUX_OUT mux_out_1 (
    .Number_1(out_11), .Number_2(out_12), .Number_3(out_13), .Number_4(out_14), .I_P(HS_le_address),
    .Number_5(out_15), .Number_6(out_16), .Number_7(out_17), .Number_8(out_18), .OUT(mux_out_1_out));
  ROM #(.dataWidth(4)) rom_1 (.addr(register_1_q), .data({CLKK, CLK, rom_1_data}));  // open: sel
  Sorted_RF sorted_rf_1 (
    .Write_Data(mux_out_1_out), .Reg_out_0(F1), .Reg_out_4(F5), .Reg_out_1(F2), .Reg_out_5(F6),
    .Reg_out_2(F3), .Reg_out_6(F7), .Reg_out_3(F4), .Reg_out_7(F8), .WriteRegister(Cur), .Clock(or_1_out),
    .clr(Clear));
  or or_1 (or_1_out, rom_1_data[1], CLK);
  Hardware_Sorter HS (
    .num1(out_11), .num2(out_12), .num3(out_13), .num4(out_14), .LE_address(HS_le_address), .num5(out_15),
    .num6(out_16), .num7(out_17), .num8(out_18), .Control(rom_1_data[0]), .CLK_EVT(rom_1_data[1]), .CLR(Clear));

  // Other names for the same wires on the sheet: CLR = Clear; O1[31:0] = out_11; O2[31:0] = out_12; O3[31:0] = out_13;
  //   O4[31:0] = out_14; O5[31:0] = out_15; O6[31:0] = out_16; O7[31:0] = out_17; O8[31:0] = out_18

  // Notes on the sheet:
  //   Unsorted memory
  //   contents of rom_1 (hex, n*v repeats v):
  //   0 8 0 8 0 8 0 8 0 8 0 8 0 8 0 8 0 3 1 3 1 4 0 2 0 2 0 4 0 2 0 2 0 4 0 2 0 2 0 4 0 2 0 2 0 4 0 2 0 2
  //   0 4 0 2 0 2 0 4 0 2 0 2 0 4
  //   INPUT
  //   OUTPUT
  //   Hardware sorter
endmodule
